# Fritzing sketch servo_knob (saved by Fritzing 1.0.1rc)
breadboards: 1

parts:
  A1 = Arduino UNO R4 WiFi
  J1 = Basic Servo
  R1 = Rotary Potentiometer (Small) [maximum_resistance=100kΩ knob_status=50% power=0.5W package=THT]

nets:
  N1: A1.Pin_8, A1.Pin_27, J1.vcc, R1.leg2
  N2: A1.Pin_9, A1.Pin_10, A1.Pin_25, A1.Pin_48, J1.gnd, R1.leg1
  N3: A1.Pin_12, R1.wiper
  N4: A1.Pin_43, J1.pulse

custom parts:
  Arduino UNO R4 WiFi: The Arduino UNO R4 WiFi merges the RA4M1 microprocessor from Renesas with the ESP32-S3 from Espressif, creating an all-in-one tool for makers with enhanced processing power and a diverse array of new peripherals.
